# Fritzing sketch Schematic (saved by Fritzing 0.9.3b)

parts:
  Part1 = Arduino Nano (Rev3.0)
  VCC1 = Battery
  IC1 = Voltage Regulator [package=to-220-alt]
  Middle = Basic Servo
  Pinky = Basic Servo
  Ring = Basic Servo
  Thumb = Basic Servo
  Index = Basic Servo
  M1 = advancer muscle sensor v3

nets:
  N1: Part1.D2, Middle.gnd, Pinky.pulse
  N2: Part1.D3, Ring.pulse
  N3: Part1.D4, Middle.pulse
  N4: Part1.D5, Index.pulse
  N5: Part1.D6, Thumb.pulse
  VIN: Part1.VIN, VCC1.+, IC1.GND
  GND: Part1.GND, VCC1.-, IC1.IN, Thumb.gnd, M1.GND
  N6: Part1.5V, M1.+Vs
  N7: Part1.A3, M1.SIG
  VCC: IC1.OUT, Middle.vcc, Thumb.vcc

custom parts:
  advancer muscle sensor v3: This sensor will measure the filtered and rectified electrical activity of a muscle; outputting 0-Vs Volts depending the amount of activity in the selected muscle, where Vs signifies the voltage of the power source. Power supply voltage: min. +-3.5V.
